// Logisim project Control-unit final.circ as structural Verilog: 1 circuit, main circuit main
module main (
  input  [2:0] OPCode,
  output SLT,
  output RegDst,
  output RegWrite,
  output ALU_SRC,
  output Mem_Read,
  output Mem_Write,
  output MemToReg,
  output Branch,
  output Jump,
  output [1:0] ALUop
);

  wire not_1_out, not_2_out, not_3_out, not_4_out, not_5_out, not_6_out, not_7_out, not_8_out, not_9_out,
       not_10_out;

  not not_1 (not_1_out, OPCode[1]);
  not not_2 (not_2_out, OPCode[2]);
  and R_type (ALUop[1], not_2_out, not_1_out, not_3_out);
  not not_3 (not_3_out, OPCode[0]);
  not not_4 (not_4_out, OPCode[1]);
  not not_5 (not_5_out, OPCode[2]);
  and LW (Mem_Read, not_5_out, not_4_out, OPCode[0]);
  not not_6 (not_6_out, OPCode[2]);
  not not_7 (not_7_out, OPCode[2]);
  not not_8 (not_8_out, OPCode[0]);
  and SW (Mem_Write, not_6_out, OPCode[1], not_8_out);
  and Beq (Branch, not_7_out, OPCode[1], OPCode[0]);
  not not_9 (not_9_out, OPCode[0]);
  not not_10 (not_10_out, OPCode[1]);
  and u_Jump (Jump, OPCode[2], not_10_out, not_9_out);
  or or_1 (ALUop[0], SLT, Branch);
  and u_SLT (SLT, OPCode[2], ~OPCode[1], OPCode[0]);  // AND_Gate
  or or_2 (RegWrite, ALUop[1], SLT, Mem_Read);
  or or_3 (ALU_SRC, Mem_Read, SLT, Mem_Write);

  assign MemToReg = Mem_Read;
  assign RegDst = ALUop[1];
endmodule
