// Logisim project maindatapathnew.circ as structural Verilog: 1 circuit, main circuit main
module main (
  input  in_1,
  input  [3:0] in_2,
  input  in_3,
  input  RESET,
  output [3:0] out_5
);

  wire and_1_out, CLK_out, main_2_alu_src, main_2_branch, main_2_jump, main_2_mem_read, main_2_mem_write,
       main_2_memtoreg, main_2_regdst, main_2_regwrite, main_2_slt, main_3_p7, multiplexer_5_out,
       n16_bit_alu_1_p5;
  wire [1:0] main_2_aluop;
  wire [2:0] multiplexer_1_out;
  wire [15:0] adder_1_out, adder_2_out, bit_extender_1_out, bit_extender_2_out, main_1_p3, main_3_p1,
       main_3_p8, multiplexer_2_out, multiplexer_3_out, multiplexer_4_out, multiplexer_7_out,
       n16_bit_alu_1_p6, PC_q, ram_1_data, rom_1_data, shifter_1_out;

  Clock CLK (.out(CLK_out));
  Register #(.width(16)) PC (.D(multiplexer_4_out), .en(in_3), .Q(PC_q), .clk(CLK_out), .clr(RESET));
  Adder #(.width(16)) adder_1 (.a(PC_q), .b(16'h1), .out(adder_1_out), .cin(in_1));  // open: cout
  ROM #(.addrWidth(16), .dataWidth(16)) rom_1 (.addr(PC_q), .data(rom_1_data));  // open: sel
  // jump_main main_1: pin names not known; wires that end beside it: adder_1_out, rom_1_data, main_1_p3
  Control_unit_final_main main_2 (
    .OPCode(rom_1_data[15:13]), .RegDst(main_2_regdst), .RegWrite(main_2_regwrite), .ALU_SRC(main_2_alu_src),
    .Mem_Read(main_2_mem_read), .Mem_Write(main_2_mem_write), .MemToReg(main_2_memtoreg),
    .Branch(main_2_branch), .Jump(main_2_jump), .ALUop(main_2_aluop), .SLT(main_2_slt));
  Shifter #(.width(16)) shifter_1 (.in(bit_extender_1_out), .\dist (in_2), .out(shifter_1_out));
  Multiplexer #(.width(3)) multiplexer_1 (
    .in0(rom_1_data[9:7]), .in1(rom_1_data[6:4]), .out(multiplexer_1_out), .sel(main_2_regdst));  // open: en
  assign bit_extender_1_out = {{9{1'b0}}, rom_1_data[6:0]};  // Bit_Extender bit_extender_1
  Adder #(.width(16)) adder_2 (.a(adder_1_out), .b(shifter_1_out), .out(adder_2_out));  // open: cin, cout
  // _8_bit_Register_file_main main_3: pin names not known; wires that end beside it: main_3_p1, rom_1_data[12:10], rom_1_data[9:7], multiplexer_1_out, CLK_out, main_2_regwrite, main_3_p7, main_3_p8, main_3_p7
  Multiplexer #(.width(16)) multiplexer_2 (
    .in0(adder_1_out), .in1(adder_2_out), .out(multiplexer_2_out), .sel(and_1_out));  // open: en
  Multiplexer #(.width(16)) multiplexer_3 (
    .in0(main_3_p8), .in1(bit_extender_1_out), .out(multiplexer_3_out), .sel(main_2_alu_src));  // open: en
  and and_1 (and_1_out, main_2_branch, n16_bit_alu_1_p5);
  Multiplexer #(.width(16)) multiplexer_4 (
    .in0(multiplexer_2_out), .in1(main_1_p3), .out(multiplexer_4_out), .sel(main_2_jump));  // open: en
  // ALU_control_main main_4: pin names not known; wires that end beside it: main_2_aluop, rom_1_data[3:0], out_5
  // _16_bit_alu 16_bit_alu_1: pin names not known; wires that end beside it: multiplexer_3_out, out_5[2], out_5[2], out_5[1:0], n16_bit_alu_1_p5, n16_bit_alu_1_p6
  Multiplexer multiplexer_5 (
    .in0(n16_bit_alu_1_p6[15]), .in1(n16_bit_alu_1_p6[15]), .out(multiplexer_5_out),
    .sel(n16_bit_alu_1_p6[15]));  // open: en
  assign bit_extender_2_out = {{15{1'b0}}, multiplexer_5_out};  // Bit_Extender bit_extender_2
  RAM #(.addrWidth(16), .dataWidth(16), .bus("separate")) ram_1 (
    .addr(n16_bit_alu_1_p6), .din(main_3_p8), .data(ram_1_data), .str(main_2_mem_write), .clk(CLK_out),
    .ld(main_2_mem_read));  // open: sel, clr
  Multiplexer #(.width(16)) multiplexer_6 (
    .in0(multiplexer_7_out), .in1(bit_extender_2_out), .out(main_3_p1), .sel(main_2_slt));  // open: en
  Multiplexer #(.width(16)) multiplexer_7 (
    .in0(n16_bit_alu_1_p6), .in1(ram_1_data), .out(multiplexer_7_out), .sel(main_2_memtoreg));  // open: en

  // Notes on the sheet:
  //   contents of rom_1 (hex, n*v repeats v):
  //   40 20 a98a 6581 8008 a40 520 8002 4202
endmodule
